// Logisim project Agustin_Carrivale - toy8-32bytes.circ as structural Verilog: 5 circuits, main circuit main
module main (
  input  [7:0] stdin,
  input  in_2,
  output [7:0] stdout
);

  wire clock_1_out, control_1_addr_mux, control_1_halt, control_1_ir_en, control_1_pc_load, control_1_r_en,
       control_1_ram_str, demultiplexer_2_out0, demultiplexer_2_out1, io_1_input, not_1_out;
  wire [1:0] control_1_aluop, control_1_r_mux;
  wire [3:0] counter_1_q, demultiplexer_1_out0, demultiplexer_1_out1, multiplexer_2_out;
  wire [7:0] alu_1_out_4, bit_extender_1_out, io_1_data_bus_2, IR_q, multiplexer_1_out, multiplexer_3_out,
       multiplexer_4_out, R_q, ram_1_data, ram_2_data;

  alu alu_1 (.ALUOp(control_1_aluop), .in_2(R_q), .in_3(multiplexer_3_out), .out_4(alu_1_out_4));
  Multiplexer #(.select(2), .width(8), .enable("false")) multiplexer_1 (
    .in0(alu_1_out_4), .in1(multiplexer_3_out), .in2(bit_extender_1_out), .out(multiplexer_1_out),
    .sel(control_1_r_mux));  // open: in3
  assign bit_extender_1_out = {{4{1'b0}}, IR_q[3:0]};  // Bit_Extender bit_extender_1
  Register #(.trigger("falling")) R (
    .D(multiplexer_1_out), .en(control_1_r_en), .Q(R_q), .clk(clock_1_out));  // open: clr
  Register IR (.D(multiplexer_3_out), .en(control_1_ir_en), .Q(IR_q), .clk(clock_1_out));  // open: clr
  not not_1 (not_1_out, control_1_pc_load);
  RAM #(.addrWidth(4), .bus("separate")) ram_1 (
    .addr(demultiplexer_1_out1), .din(R_q), .data(ram_1_data), .str(demultiplexer_2_out1),
    .clk(demultiplexer_2_out1));  // open: sel, ld, clr
  Counter #(.width(4), .max('hf), .trigger("falling")) counter_1 (
    .load(control_1_pc_load), .D(IR_q[3:0]), .count(not_1_out), .Q(counter_1_q), .clk(clock_1_out));  // open: carry, clr
  Multiplexer #(.width(4), .enable("false")) multiplexer_2 (
    .in0(counter_1_q), .in1(IR_q[3:0]), .out(multiplexer_2_out), .sel(control_1_addr_mux));
  control control_1 (
    .CLK(clock_1_out), .Opcode(IR_q[7:5]), .in_3(R_q), .halt(control_1_halt), .IR_en(control_1_ir_en),
    .R_en(control_1_r_en), .RAM_str(control_1_ram_str), .PC_load(control_1_pc_load),
    .ADDR_MUX(control_1_addr_mux), .R_MUX(control_1_r_mux), .ALUOp(control_1_aluop));
  Demultiplexer #(.width(4), .enable("false")) demultiplexer_1 (
    .out0(demultiplexer_1_out0), .out1(demultiplexer_1_out1), .in(multiplexer_2_out), .sel(control_1_addr_mux));
  RAM #(.addrWidth(4), .bus("separate")) ram_2 (
    .addr(demultiplexer_1_out0), .din(R_q), .data(ram_2_data), .str(demultiplexer_2_out0),
    .clk(demultiplexer_2_out0));  // open: sel, ld, clr
  Multiplexer #(.width(8), .enable("false")) multiplexer_3 (
    .in0(multiplexer_4_out), .in1(io_1_data_bus_2), .out(multiplexer_3_out), .sel(io_1_input));
  Demultiplexer #(.enable("false")) demultiplexer_2 (
    .out0(demultiplexer_2_out0), .out1(demultiplexer_2_out1), .in(control_1_ram_str), .sel(control_1_addr_mux));
  clock clock_1 (.RUN(in_2), .HALT(control_1_halt), .OUT(clock_1_out));
  io io_1 (
    .stdin(stdin), .address_bus(multiplexer_2_out), .data_bus_2(io_1_data_bus_2), .stdout(stdout),
    .\input (io_1_input), .clk(clock_1_out));  // open: data_bus
  Multiplexer #(.width(8), .enable("false")) multiplexer_4 (
    .in0(ram_2_data), .in1(ram_1_data), .out(multiplexer_4_out), .sel(control_1_addr_mux));

  // Notes on the sheet:
  //   PC
  //   RAM
endmodule

module alu (
  input  [1:0] ALUOp,
  input  [7:0] in_2,
  input  [7:0] in_3,
  output [7:0] out_4
);

  wire [7:0] adder_1_out, and_1_out, xor_1_out;

  Adder adder_1 (.a(in_2), .b(in_3), .out(adder_1_out));  // open: cin, cout
  assign and_1_out = in_2 & in_3;  // AND_Gate and_1, 8 bits wide
  assign xor_1_out = in_2 ^ in_3;  // XOR_Gate xor_1, 8 bits wide
  Multiplexer #(.select(2), .width(8), .enable("false")) multiplexer_1 (
    .in0(adder_1_out), .in1(and_1_out), .in2(xor_1_out), .out(out_4), .sel(ALUOp));  // open: in3

  // Notes on the sheet:
  //   A
  //   B
  //   R
endmodule

module control (
  input  CLK,
  input  [2:0] Opcode,
  input  [7:0] in_3,
  output halt,
  output IR_en,
  output R_en,
  output RAM_str,
  output PC_load,
  output ADDR_MUX,
  output [1:0] R_MUX,
  output [1:0] ALUOp
);

  wire and_1_out, demultiplexer_1_out1, demultiplexer_1_out7;
  wire [7:0] not_1_out;

  assign not_1_out = ~in_3;  // NOT_Gate not_1, 8 bits wide
  Demultiplexer #(.select(3), .enable("false")) demultiplexer_1 (
    .out0(halt), .out1(demultiplexer_1_out1), .out2(ALUOp[0]), .out3(ALUOp[1]), .out4(R_MUX[1]),
    .out5(R_MUX[0]), .out6(RAM_str), .out7(demultiplexer_1_out7), .in(CLK), .sel(Opcode));
  and and_1 (and_1_out, not_1_out[0], not_1_out[1], not_1_out[2], not_1_out[3], not_1_out[4], not_1_out[5], not_1_out[6], not_1_out[7]);
  or or_1 (R_en, demultiplexer_1_out1, ALUOp[0], ALUOp[1], R_MUX[1], R_MUX[0]);
  and and_2 (PC_load, demultiplexer_1_out7, and_1_out);
  not not_2 (IR_en, CLK);

  assign ADDR_MUX = CLK;

  // Notes on the sheet:
  //   R
endmodule

module clock (
  input  RUN,
  input  HALT,
  output OUT
);

  wire clock_1_out, xor_1_out;

  Clock clock_1 (.out(clock_1_out));
  D_Flip_Flop #(.trigger("high")) d_ff_1 (
    .clk(1'b1), .D(clock_1_out), .Q(OUT), .en(xor_1_out));  // open: Qn, preset, reset
  xor xor_1 (xor_1_out, RUN, HALT);
endmodule

module io (
  input  clk,
  input  [7:0] stdin,
  input  [7:0] data_bus,
  input  [3:0] address_bus,
  output [7:0] data_bus_2,
  output [7:0] stdout,
  output \input 
);

  and and_1 (\input , address_bus[0], address_bus[1], address_bus[2], address_bus[3]);
  Register #(.trigger("high")) input_register (.D(stdin), .en(\input ), .Q(data_bus_2), .clk(clk));  // open: clr
  Register #(.trigger("falling")) output_register (.D(data_bus), .en(\input ), .Q(stdout), .clk(clk));  // open: clr
endmodule
